// Logisim project Data Fetching.circ as structural Verilog
module main (
  input  in_1,
  input  in_2,
  output [31:0] out_3,
  output [31:0] out_4,
  output [31:0] out_5
);

  wire clock_1_out, undriven;
  wire [1:0] immediate_datapath_1_selbit_for_mux;
  wire [23:0] bit_extender_1_out;
  wire [31:0] adder_2_out, IMM_FORB_TYPE, immediate_datapath_1_rs1_immedi_for_jalr, multiplexer_1_out,
       pc_for_auipc, ram_1_data, shifter_1_out;

  Adder #(.width(32)) adder_1 (.a(32'h4), .b(pc_for_auipc), .out(out_4));  // open: cin, cout
  Multiplexer #(.select(2), .width(32)) multiplexer_1 (
    .in0(out_4), .in1(adder_2_out), .in2(immediate_datapath_1_rs1_immedi_for_jalr), .in3(adder_2_out),
    .out(multiplexer_1_out), .sel(immediate_datapath_1_selbit_for_mux));  // open: en
  Clock clock_1 (.out(clock_1_out));
  Adder #(.width(32)) adder_2 (.a(pc_for_auipc), .b(IMM_FORB_TYPE), .out(adder_2_out));  // open: cin, cout
  Register #(.width(32)) register_1 (
    .D(multiplexer_1_out), .en(undriven), .Q(pc_for_auipc), .clk(clock_1_out), .clr(in_2));
  Shifter #(.width(32), .shift("lr")) shifter_1 (.in(pc_for_auipc), .\dist (5'b00010), .out(shifter_1_out));
  Bit_Extender #(.in_width(32), .out_width(24)) bit_extender_1 (.in(shifter_1_out), .out(bit_extender_1_out));
  RAM #(.addrWidth(24), .dataWidth(32)) ram_1 (
    .addr(bit_extender_1_out), .data(ram_1_data), .clk(clock_1_out));  // open: sel, ld, clr
  immediate_datapath immediate_datapath_1 (
    .store(in_1), .Inputinstruction(ram_1_data), .reset_for_reg_file(in_2), .clk(clock_1_out), .pc_4(out_4),
    .pc_for_auipc(pc_for_auipc), .ram_data(out_3), .reset(in_2),
    .rs1_immedi_for_jalr(immediate_datapath_1_rs1_immedi_for_jalr), .rd(out_5),
    .Selbit_for_mux(immediate_datapath_1_selbit_for_mux), .IMM_FOR_b_TYPE(IMM_FORB_TYPE));  // open: enable_for_imm_jal_branch

  // Other names for the same wires on the sheet: pc_4[31:0] = out_4
endmodule

module R_Type_inst (
  input  [31:0] in_1,
  output [2:0] Funct3,
  output [6:0] Opcode,
  output [4:0] RD,
  output [4:0] RS1,
  output [4:0] RS2,
  output [6:0] Funct7
);


  assign Funct3 = in_1[14:12];
  assign Funct7 = in_1[31:25];
  assign Opcode = in_1[6:0];
  assign RD = in_1[11:7];
  assign RS1 = in_1[19:15];
  assign RS2 = in_1[24:20];

  // Notes on the sheet:
  //   R_Type
endmodule

// Immediate generator
module Immediate_Generator (
  input  [31:0] Inst_Input,
  output [31:0] Immediate
);

  wire comparator_1_eq, comparator_2_eq, comparator_3_eq, comparator_4_eq, comparator_5_eq, comparator_6_eq,
       comparator_7_eq, comparator_8_eq, comparator_9_eq;
  wire [3:0] b_type_immediate_1_imm_4_1, priority_encoder_1_out;
  wire [4:0] s_type_immediate_1_imm_4_0;
  wire [5:0] b_type_immediate_1_imm_10_5;
  wire [6:0] b_type_immediate_1_out_2, i_type_immediate_1_out_2, i_type_immediate_2_out_2,
       i_type_immediate_3_out_2, j_type_immediate_1_out_2, r_type_inst_1_opcode, s_type_immediate_1_out_2,
       s_type_immediate_1_out_7, u_type_immediate_1_out_2, u_type_immediate_2_out_2;
  wire [7:0] j_type_immediate_1_imm12_19;
  wire [9:0] j_type_immediate_1_imm1_10;
  wire [11:0] i_type_immediate_1_imm, i_type_immediate_2_imm, i_type_immediate_3_imm;
  wire [12:11] b_type_immediate_1_imm_11;
  wire [20:11] j_type_immediate_1_imm11;
  wire [31:0] B_Type, I_Type, I_Typefor_lw, J_Type, jalr, S_Type;
  wire [31:12] auipc, U_Type;

  Bit_Extender #(.in_width(20), .out_width(32)) bit_extender_1 ();  // open: in, out
  B_Type_Immediate b_type_immediate_1 (
    .in_1(Inst_Input), .out_2(b_type_immediate_1_out_2), .imm_11(b_type_immediate_1_imm_11[11]),
    .IMM_4_1(b_type_immediate_1_imm_4_1), .IMM_10_5(b_type_immediate_1_imm_10_5),
    .imm_12(b_type_immediate_1_imm_11[12]));  // open: Funct_3, rs1, rs2
  J_Type_Immediate j_type_immediate_1 (
    .in_1(Inst_Input), .out_2(j_type_immediate_1_out_2), .imm12_19(j_type_immediate_1_imm12_19),
    .imm11(j_type_immediate_1_imm11[11]), .imm1_10(j_type_immediate_1_imm1_10),
    .imm20(j_type_immediate_1_imm11[20]));  // open: RD
  U_Type_Immediate u_type_immediate_1 (
    .in_1(Inst_Input), .out_2(u_type_immediate_1_out_2), .out_4(U_Type));  // open: RD
  I_Type_Immediate i_type_immediate_1 (
    .in_1(Inst_Input), .out_2(i_type_immediate_1_out_2), .imm(i_type_immediate_1_imm));  // open: rd, funct3, rs1
  S_Type_Immediate s_type_immediate_1 (
    .in_1(Inst_Input), .out_2(s_type_immediate_1_out_2), .IMM_4_0(s_type_immediate_1_imm_4_0),
    .out_7(s_type_immediate_1_out_7));  // open: Funct3, RS1, RS2
  R_Type_inst r_type_inst_1 (.in_1(Inst_Input), .Opcode(r_type_inst_1_opcode));  // open: Funct3, RD, RS1, RS2, Funct7
  I_Type_Immediate i_type_immediate_2 (
    .in_1(Inst_Input), .out_2(i_type_immediate_2_out_2), .imm(i_type_immediate_2_imm));  // open: rd, funct3, rs1
  assign I_Type = {{20{1'b0}}, i_type_immediate_1_imm};  // Bit_Extender bit_extender_2
  Comparator #(.width(7)) comparator_1 (
    .a(r_type_inst_1_opcode), .b(7'b0110011), .eq(comparator_1_eq));  // open: gt, lt
  assign jalr = {{20{1'b0}}, i_type_immediate_2_imm};  // Bit_Extender bit_extender_3
  Comparator #(.width(7)) comparator_2 (
    .a(i_type_immediate_1_out_2), .b(7'b0010011), .eq(comparator_2_eq));  // open: gt, lt
  Comparator #(.width(7)) comparator_3 (
    .a(s_type_immediate_1_out_2), .b(7'b0100011), .eq(comparator_3_eq));  // open: gt, lt
  assign S_Type = {{20{1'b0}}, {s_type_immediate_1_out_7, s_type_immediate_1_imm_4_0}};  // Bit_Extender bit_extender_4
  Comparator #(.width(7)) comparator_4 (
    .a(b_type_immediate_1_out_2), .b(7'b1100011), .eq(comparator_4_eq));  // open: gt, lt
  assign B_Type = {{19{1'b0}}, {b_type_immediate_1_imm_11, b_type_immediate_1_imm_10_5, b_type_immediate_1_imm_4_1, 1'b0}};  // Bit_Extender bit_extender_5
  Comparator #(.width(7)) comparator_5 (
    .a(j_type_immediate_1_out_2), .b(7'b1101111), .eq(comparator_5_eq));  // open: gt, lt
  assign J_Type = {{11{1'b0}}, {j_type_immediate_1_imm11[20], j_type_immediate_1_imm12_19, j_type_immediate_1_imm11[11], j_type_immediate_1_imm1_10, 1'b0}};  // Bit_Extender bit_extender_6
  Comparator #(.width(7)) comparator_6 (
    .a(u_type_immediate_1_out_2), .b(7'b0110111), .eq(comparator_6_eq));  // open: gt, lt
  Comparator #(.width(7)) comparator_7 (
    .a(i_type_immediate_2_out_2), .b(7'b1100111), .eq(comparator_7_eq));  // open: gt, lt
  I_Type_Immediate i_type_immediate_3 (
    .in_1(Inst_Input), .out_2(i_type_immediate_3_out_2), .imm(i_type_immediate_3_imm));  // open: rd, funct3, rs1
  assign I_Typefor_lw = {{20{1'b0}}, i_type_immediate_3_imm};  // Bit_Extender bit_extender_7
  U_Type_Immediate u_type_immediate_2 (.in_1(Inst_Input), .out_2(u_type_immediate_2_out_2), .out_4(auipc));  // open: RD
  Comparator #(.width(7)) comparator_8 (
    .a(i_type_immediate_3_out_2), .b(7'b0000011), .eq(comparator_8_eq));  // open: gt, lt
  Multiplexer #(.select(4), .width(32)) multiplexer_1 (
    .in0(I_Type), .in1(S_Type), .in2(B_Type), .in3(J_Type), .in4({U_Type, {12{1'b0}}}), .in5({32{1'b0}}),
    .in6(I_Typefor_lw), .in7(jalr), .in8({auipc, {12{1'b0}}}), .out(Immediate), .sel(priority_encoder_1_out));  // open: in9, in10, in11, in12, in13, in14, in15, en
  Comparator #(.width(7)) comparator_9 (
    .a(u_type_immediate_2_out_2), .b(7'b0010111), .eq(comparator_9_eq));  // open: gt, lt
  Priority_Encoder #(.select(4)) priority_encoder_1 (
    .in0(comparator_2_eq), .in1(comparator_3_eq), .in2(comparator_4_eq), .in3(comparator_5_eq),
    .in4(comparator_6_eq), .in5(comparator_1_eq), .in6(comparator_8_eq), .in7(comparator_7_eq),
    .in8(comparator_9_eq), .out(priority_encoder_1_out));  // open: in9, in10, in11, in12, in13, in14, in15, gs, en_out, en_in

  // Other names for the same wires on the sheet: Input[31:0] = Inst_Input
endmodule

module Register_File (
  input  [4:0] RSI,
  input  [4:0] RSI2,
  input  [4:0] RDInstruction,
  input  reset,
  input  clk,
  input  [31:0] RDValue,
  input  Write_Enable,
  output [31:0] RS1out,
  output [31:0] RS2out
);

  wire x0, x1, x2, x3, x4, x5, x6, x7, x8, x9, x10, x11, x12, x13, x14, x15, x16, x17, x18, x19, x20, x21,
       x22, x23, x24, x25, x26, x27, x28, x29, x30, x31;
  wire [31:0] x0out, x1out, x2out, x3out, x4out, x5out, x6out, x7out, x8out, x9out, x10out, x11out, x12out,
       x14out, x16out, x17out, x18out, x19out, x20out, x21out, x22out, x23out, x24out, x25out, x26out,
       x27out, x28out, x29out, x30out, x31out;

  Demultiplexer #(.select(5)) demultiplexer_1 (
    .out0(x0), .out1(x1), .out2(x2), .out3(x3), .out4(x4), .out5(x5), .out6(x6), .out7(x7), .out8(x8),
    .out9(x9), .out10(x10), .out11(x11), .out12(x12), .out13(x13), .out14(x14), .out15(x15), .out16(x16),
    .out17(x17), .out18(x18), .out19(x19), .out20(x20), .out21(x21), .out22(x22), .out23(x23), .out24(x24),
    .out25(x25), .out26(x26), .out27(x27), .out28(x28), .out29(x29), .out30(x30), .out31(x31),
    .in(Write_Enable), .sel(RDInstruction));  // open: en
  Register #(.width(32)) u_X0 (.D(RDValue), .en(x0), .Q(x0out), .clk(clk), .clr(reset));
  Register #(.width(32)) u_X4 (.D(RDValue), .en(x4), .Q(x4out), .clk(clk), .clr(reset));
  Register #(.width(32)) u_X8 (.D(RDValue), .en(x8), .Q(x8out), .clk(clk), .clr(reset));
  Register #(.width(32)) u_X12 (.D(RDValue), .en(x12), .Q(x12out), .clk(clk), .clr(reset));
  Register #(.width(32)) u_X16 (.D(RDValue), .en(x16), .Q(x16out), .clk(clk), .clr(reset));
  Register #(.width(32)) u_X20 (.D(RDValue), .en(x20), .Q(x20out), .clk(clk), .clr(reset));
  Register #(.width(32)) u_X24 (.D(RDValue), .en(x24), .Q(x24out), .clk(clk), .clr(reset));
  Register #(.width(32)) u_X28 (.D(RDValue), .en(x28), .Q(x28out), .clk(clk), .clr(reset));
  Register #(.width(32)) u_X1 (.D(RDValue), .en(x1), .Q(x1out), .clk(clk), .clr(reset));
  Register #(.width(32)) u_X5 (.D(RDValue), .en(x5), .Q(x5out), .clk(clk), .clr(reset));
  Register #(.width(32)) u_X9 (.D(RDValue), .en(x9), .Q(x9out), .clk(clk), .clr(reset));
  Register #(.width(32)) u_X13 (.D(RDValue), .en(x13), .Q(x12out), .clk(clk), .clr(reset));
  Register #(.width(32)) u_X17 (.D(RDValue), .en(x17), .Q(x17out), .clk(clk), .clr(reset));
  Register #(.width(32)) u_X21 (.D(RDValue), .en(x21), .Q(x21out), .clk(clk), .clr(reset));
  Register #(.width(32)) u_X25 (.D(RDValue), .en(x25), .Q(x25out), .clk(clk), .clr(reset));
  Register #(.width(32)) u_X29 (.D(RDValue), .en(x29), .Q(x29out), .clk(clk), .clr(reset));
  Register #(.width(32)) u_X2 (.D(RDValue), .en(x2), .Q(x2out), .clk(clk), .clr(reset));
  Register #(.width(32)) u_X6 (.D(RDValue), .en(x6), .Q(x6out), .clk(clk), .clr(reset));
  Register #(.width(32)) u_X10 (.D(RDValue), .en(x10), .Q(x10out), .clk(clk), .clr(reset));
  Register #(.width(32)) u_X14 (.D(RDValue), .en(x14), .Q(x14out), .clk(clk), .clr(reset));
  Register #(.width(32)) u_X18 (.D(RDValue), .en(x18), .Q(x18out), .clk(clk), .clr(reset));
  Register #(.width(32)) u_X22 (.D(RDValue), .en(x22), .Q(x22out), .clk(clk), .clr(reset));
  Register #(.width(32)) u_X26 (.D(RDValue), .en(x26), .Q(x26out), .clk(clk), .clr(reset));
  Register #(.width(32)) u_X30 (.D(RDValue), .en(x30), .Q(x30out), .clk(clk), .clr(reset));
  Register #(.width(32)) u_X3 (.D(RDValue), .en(x3), .Q(x3out), .clk(clk), .clr(reset));
  Register #(.width(32)) u_X7 (.D(RDValue), .en(x7), .Q(x7out), .clk(clk), .clr(reset));
  Register #(.width(32)) u_X11 (.D(RDValue), .en(x11), .Q(x11out), .clk(clk), .clr(reset));
  Register #(.width(32)) u_X15 (.D(RDValue), .en(x15), .Q(x14out), .clk(clk), .clr(reset));
  Register #(.width(32)) u_X19 (.D(RDValue), .en(x19), .Q(x19out), .clk(clk), .clr(reset));
  Register #(.width(32)) u_X23 (.D(RDValue), .en(x23), .Q(x23out), .clk(clk), .clr(reset));
  Register #(.width(32)) u_X27 (.D(RDValue), .en(x27), .Q(x27out), .clk(clk), .clr(reset));
  Register #(.width(32)) u_X31 (.D(RDValue), .en(x31), .Q(x31out), .clk(clk), .clr(reset));
  Multiplexer #(.select(5), .width(32)) multiplexer_1 (
    .in0(x0out), .in1(x1out), .in2(x2out), .in3(x3out), .in4(x4out), .in5(x5out), .in6(x6out), .in7(x7out),
    .in8(x8out), .in9(x9out), .in10(x10out), .in11(x11out), .in12(x12out), .in13(x12out), .in14(x14out),
    .in15(x14out), .in16(x16out), .in17(x17out), .in18(x18out), .in19(x19out), .in20(x20out), .in21(x21out),
    .in22(x22out), .in23(x23out), .in24(x24out), .in25(x25out), .in26(x26out), .in27(x27out), .in28(x28out),
    .in29(x29out), .in30(x30out), .in31(x31out), .out(RS1out), .sel(RSI));  // open: en
  Multiplexer #(.select(5), .width(32)) multiplexer_2 (
    .in0(x0out), .in1(x1out), .in2(x2out), .in3(x3out), .in4(x4out), .in5(x5out), .in6(x6out), .in7(x7out),
    .in8(x8out), .in9(x9out), .in10(x10out), .in11(x11out), .in12(x12out), .in13(x12out), .in14(x14out),
    .in15(x14out), .in16(x16out), .in17(x17out), .in18(x18out), .in19(x19out), .in20(x20out), .in21(x21out),
    .in22(x22out), .in23(x23out), .in24(x24out), .in25(x25out), .in26(x26out), .in27(x27out), .in28(x28out),
    .in29(x29out), .in30(x30out), .in31(x31out), .out(RS2out), .sel(RSI2));  // open: en

  // Other names for the same wires on the sheet: RDI[4:0] = RDInstruction; RSI1[4:0] = RSI; W_E = Write_Enable;
  //   x13out[31:0] = x12out; x15out[31:0] = x14out
endmodule

module PC (
  input  in_1,
  input  [31:0] in_2,
  input  in_3,
  input  [4:0] in_4,
  output [31:0] out_5,
  output out_6
);

  wire clock_1_out, undriven;
  wire [23:0] bit_extender_1_out;
  wire [31:0] register_1_q, shifter_1_out;

  Adder #(.width(32)) adder_1 (.a(in_2), .b(register_1_q), .out(out_5), .cin(in_1), .cout(out_6));
  Clock clock_1 (.out(clock_1_out));
  Register #(.width(32)) register_1 (.D(out_5), .en(undriven), .Q(register_1_q), .clk(clock_1_out), .clr(in_3));
  Shifter #(.width(32), .shift("lr")) shifter_1 (.in(register_1_q), .\dist (in_4), .out(shifter_1_out));
  Bit_Extender #(.in_width(32), .out_width(24)) bit_extender_1 (.in(shifter_1_out), .out(bit_extender_1_out));
  RAM #(.addrWidth(24), .dataWidth(32)) ram_1 (
    .addr(bit_extender_1_out), .clk(clock_1_out));  // open: data, sel, ld, clr
endmodule

module I_Type_Immediate (
  input  [31:0] in_1,
  output [6:0] out_2,
  output [4:0] rd,
  output [2:0] funct3,
  output [4:0] rs1,
  output [11:0] imm
);


  assign funct3 = in_1[14:12];
  assign imm = in_1[31:20];
  assign out_2 = in_1[6:0];
  assign rd = in_1[11:7];
  assign rs1 = in_1[19:15];

  // Notes on the sheet:
  //   Opcode
endmodule

module S_Type_Immediate (
  input  [31:0] in_1,
  output [6:0] out_2,
  output [4:0] IMM_4_0,
  output [2:0] Funct3,
  output [4:0] RS1,
  output [4:0] RS2,
  output [6:0] out_7
);


  assign Funct3 = in_1[14:12];
  assign IMM_4_0 = in_1[11:7];
  assign out_2 = in_1[6:0];
  assign out_7 = in_1[31:25];
  assign RS1 = in_1[19:15];
  assign RS2 = in_1[24:20];

  // Notes on the sheet:
  //   OPCODE
  //   IMM[31:25]
endmodule

module B_Type_Immediate (
  input  [31:0] in_1,
  output [6:0] out_2,
  output imm_11,
  output [3:0] IMM_4_1,
  output [2:0] Funct_3,
  output [4:0] rs1,
  output [4:0] rs2,
  output [5:0] IMM_10_5,
  output imm_12
);


  assign Funct_3 = in_1[14:12];
  assign IMM_4_1 = in_1[11:8];
  assign IMM_10_5 = in_1[30:25];
  assign imm_11 = in_1[7];
  assign imm_12 = in_1[31];
  assign out_2 = in_1[6:0];
  assign rs1 = in_1[19:15];
  assign rs2 = in_1[24:20];

  // Notes on the sheet:
  //   Opcode
endmodule

module J_Type_Immediate (
  input  [31:0] in_1,
  output [6:0] out_2,
  output [4:0] RD,
  output [7:0] imm12_19,
  output imm11,
  output [9:0] imm1_10,
  output imm20
);


  assign imm1_10 = in_1[30:21];
  assign imm11 = in_1[20];
  assign imm12_19 = in_1[19:12];
  assign imm20 = in_1[31];
  assign out_2 = in_1[6:0];
  assign RD = in_1[11:7];

  // Notes on the sheet:
  //   OPCODE
  //   IMM[19:12]
  //   IMM[11]
  //   IMM[10:1]
  //   IMM[20]
endmodule

module U_Type_Immediate (
  input  [31:0] in_1,
  output [6:0] out_2,
  output [4:0] RD,
  output [19:0] out_4
);


  assign out_2 = in_1[6:0];
  assign out_4 = in_1[31:12];
  assign RD = in_1[11:7];

  // Notes on the sheet:
  //   Opcode
  //   IMM[31:12]
endmodule

module DataPath (
  input  [31:0] in_1,
  output [31:0] out_2,
  output [31:0] out_3
);

  wire clock_1_out, register_file_1_p6;
  wire [3:0] control_unit_1_p2;
  wire [4:0] r_type_inst_1_rd, r_type_inst_1_rs1, r_type_inst_1_rs2;
  wire [31:0] register_file_1_p8;

  Clock clock_1 (.out(clock_1_out));
  R_Type_inst r_type_inst_1 (
    .in_1(in_1), .RD(r_type_inst_1_rd), .RS1(r_type_inst_1_rs1), .RS2(r_type_inst_1_rs2));  // open: Funct3, Opcode, Funct7
  // Register_File register_file_1: pin names not known; wires that end beside it: r_type_inst_1_rs1, r_type_inst_1_rs2, r_type_inst_1_rd, clock_1_out, out_3, register_file_1_p6, out_2, register_file_1_p8
  // Control_Unit control_unit_1: pin names not known; wires that end beside it: in_1, control_unit_1_p2, register_file_1_p6, register_file_1_p6
  ALU alu_1 (
    .dataA(out_2), .dataB(register_file_1_p8), .selector(control_unit_1_p2), .dataD(out_3));  // open: selbit_for_unsigned, output_branch_taken

  // Notes on the sheet:
  //   00418133
endmodule

module ALU (
  input  [31:0] dataA,
  input  [31:0] dataB,
  input  [3:0] selector,
  input  selbit_for_unsigned,
  output [31:0] dataD,
  output output_branch_taken
);

  wire branch_1_bge_u, branch_1_blt_u, branch_1_breq, comparator_1_lt, comparator_2_lt, comparator_3_eq,
       undriven;
  wire [31:0] adderout, andout, orout, sll, slt, sltunsigned, sra, srl, subtout, xorout;

  Adder #(.width(32)) adder_1 (.a(dataA), .b(dataB), .out(adderout));  // open: cin, cout
  Subtractor #(.width(32)) subtractor_1 (.a(dataA), .b(dataB), .out(subtout));  // open: bin, bout
  Shifter #(.width(32)) shifter_1 (.in(dataA), .\dist (dataB[4:0]), .out(sll));
  Comparator #(.width(32)) comparator_1 (.a(dataA), .b(dataB), .lt(comparator_1_lt));  // open: gt, eq
  Comparator #(.width(32), .mode("unsigned")) comparator_2 (
    .a(dataA), .b(dataB), .lt(comparator_2_lt));  // open: gt, eq
  assign xorout = dataA ^ dataB;  // XOR_Gate xor_1, 32 bits wide
  assign andout = dataA & dataB;  // AND_Gate and_1, 32 bits wide
  assign orout = dataA | dataB;  // OR_Gate or_1, 32 bits wide
  Shifter #(.width(32), .shift("lr")) shifter_2 (.in(dataA), .\dist (dataB[4:0]), .out(srl));
  Shifter #(.width(32), .shift("ar")) shifter_3 (.in(dataA), .\dist (dataB[4:0]), .out(sra));
  assign slt = {{31{1'b0}}, comparator_1_lt};  // Bit_Extender bit_extender_1
  assign sltunsigned = {{31{1'b0}}, comparator_2_lt};  // Bit_Extender bit_extender_2
  Branch branch_1 (
    .dataA(dataA), .dataB(dataB), .\unsigned (selbit_for_unsigned), .blt_u(branch_1_blt_u),
    .Breq(branch_1_breq), .bge_u(branch_1_bge_u));
  Multiplexer #(.select(4), .width(32)) multiplexer_1 (
    .in0(adderout), .in1(sll), .in2(slt), .in3(sltunsigned), .in4(xorout), .in5(srl), .in6(orout),
    .in7(andout), .in8(subtout), .in13(sra), .out(dataD), .sel(selector));  // open: in9, in10, in11, in12, in14, in15, en
  Comparator #(.width(1)) comparator_3 (.a(undriven), .b(1'b1), .eq(comparator_3_eq));  // open: gt, lt
  or or_2 (output_branch_taken, branch_1_blt_u, branch_1_breq, branch_1_bge_u);

  // Other names for the same wires on the sheet: dataAi[31:0] = dataA; dataBi[31:0] = dataB;
  //   dataBshift[4:0] = dataB[4:0]
endmodule

module Branch (
  input  [31:0] dataA,
  input  [31:0] dataB,
  input  \unsigned ,
  output blt_u,
  output Breq,
  output bge_u
);

  wire comparator_1_gt, comparator_1_lt, comparator_2_eq, comparator_2_gt, comparator_2_lt, or_1_out,
       or_2_out;

  Comparator #(.width(32)) comparator_1 (.a(dataA), .b(dataB), .gt(comparator_1_gt), .eq(Breq), .lt(comparator_1_lt));
  Comparator #(.width(32), .mode("unsigned")) comparator_2 (
    .a(dataA), .b(dataB), .gt(comparator_2_gt), .eq(comparator_2_eq), .lt(comparator_2_lt));
  Multiplexer multiplexer_1 (.in0(comparator_1_lt), .in1(comparator_2_lt), .out(blt_u), .sel(\unsigned ));  // open: en
  or or_1 (or_1_out, comparator_2_gt, comparator_2_eq);
  or or_2 (or_2_out, comparator_1_gt, Breq);
  Multiplexer multiplexer_2 (.in0(or_2_out), .in1(or_1_out), .out(bge_u), .sel(\unsigned ));  // open: en

  // Notes on the sheet:
  //   blt
  //   bltu
endmodule

// CU
module Control_Unit (
  input  [31:0] Instruction,
  output [3:0] SelBit,
  output wenb,
  output rs2_imm_sel,
  output Enable_for_jal,
  output Load_Enable,
  output Branch_enable,
  output enable_for_auipc,
  output [1:0] selbit_for_mux,
  output lui_enable
);

  wire Add, Addi, Addr, And, Andi, Andr, Bge, Bgeu, Blt, Bltu, Bne, Breq, jal, jalr, lb, lbu, lh, lhu, lw,
       nor_1_out, OR, ORi, ORr, sb, sh, Sll, Slli, Sllr, Slt, Slti, Sltr, Sltu, Sltui, Sltur, Sra, Srai,
       Srar, Srl, Srli, Srlr, Sub, sw, Xor, Xori, Xorr;

  or or_1 (Load_Enable, lb, lh, lw, lbu, lhu);
  and and_1 (sw, ~Instruction[2], ~Instruction[3], ~Instruction[4], Instruction[5], ~Instruction[6], ~Instruction[12], Instruction[13], ~Instruction[14], ~Instruction[30]);  // AND_Gate
  and and_2 (sh, ~Instruction[2], ~Instruction[3], ~Instruction[4], Instruction[5], ~Instruction[6], Instruction[12], ~Instruction[13], ~Instruction[14], ~Instruction[30]);  // AND_Gate
  and and_3 (sb, ~Instruction[2], ~Instruction[3], ~Instruction[4], Instruction[5], ~Instruction[6], ~Instruction[12], ~Instruction[13], ~Instruction[14], ~Instruction[30]);  // AND_Gate
  and and_4 (lb, ~Instruction[2], ~Instruction[3], ~Instruction[4], ~Instruction[5], ~Instruction[6], ~Instruction[12], ~Instruction[13], ~Instruction[14], ~Instruction[30]);  // AND_Gate
  and and_5 (lh, ~Instruction[2], ~Instruction[3], ~Instruction[4], ~Instruction[5], ~Instruction[6], Instruction[12], ~Instruction[13], ~Instruction[14], ~Instruction[30]);  // AND_Gate
  and and_6 (lw, ~Instruction[2], ~Instruction[3], ~Instruction[4], ~Instruction[5], ~Instruction[6], ~Instruction[12], Instruction[13], ~Instruction[14], ~Instruction[30]);  // AND_Gate
  and and_7 (lbu, ~Instruction[2], ~Instruction[3], ~Instruction[4], ~Instruction[5], ~Instruction[6], ~Instruction[12], ~Instruction[13], Instruction[14], ~Instruction[30]);  // AND_Gate
  and and_8 (lhu, ~Instruction[2], ~Instruction[3], ~Instruction[4], ~Instruction[5], ~Instruction[6], Instruction[12], ~Instruction[13], Instruction[14], ~Instruction[30]);  // AND_Gate
  and and_9 (jal, Instruction[2], Instruction[3], ~Instruction[4], Instruction[5], Instruction[6], ~Instruction[12], ~Instruction[13], ~Instruction[14], ~Instruction[30]);  // AND_Gate
  and and_10 (jalr, Instruction[2], ~Instruction[3], ~Instruction[4], Instruction[5], Instruction[6], ~Instruction[12], ~Instruction[13], ~Instruction[14], ~Instruction[30]);  // AND_Gate
  or or_2 (Enable_for_jal, jal, jalr);
  and and_11 (enable_for_auipc, Instruction[2], ~Instruction[3], Instruction[4], ~Instruction[5], ~Instruction[6]);  // AND_Gate
  and and_12 (lui_enable, Instruction[2], ~Instruction[3], Instruction[4], Instruction[5], ~Instruction[6]);  // AND_Gate
  and and_13 (Addr, ~Instruction[2], ~Instruction[3], Instruction[4], Instruction[5], ~Instruction[6], ~Instruction[12], ~Instruction[13], ~Instruction[14], ~Instruction[30]);  // AND_Gate
  and and_14 (Sub, ~Instruction[2], ~Instruction[3], Instruction[4], Instruction[5], ~Instruction[6], ~Instruction[12], ~Instruction[13], ~Instruction[14], Instruction[30]);  // AND_Gate
  and and_15 (Sllr, ~Instruction[2], ~Instruction[3], Instruction[4], Instruction[5], ~Instruction[6], Instruction[12], ~Instruction[13], ~Instruction[14], ~Instruction[30]);  // AND_Gate
  and and_16 (Sltr, ~Instruction[2], ~Instruction[3], Instruction[4], Instruction[5], ~Instruction[6], ~Instruction[12], Instruction[13], ~Instruction[14], ~Instruction[30]);  // AND_Gate
  and and_17 (Sltur, ~Instruction[2], ~Instruction[3], Instruction[4], Instruction[5], ~Instruction[6], Instruction[12], Instruction[13], ~Instruction[14], ~Instruction[30]);  // AND_Gate
  and and_18 (Xorr, ~Instruction[2], ~Instruction[3], Instruction[4], Instruction[5], ~Instruction[6], ~Instruction[12], ~Instruction[13], Instruction[14], ~Instruction[30]);  // AND_Gate
  and and_19 (Srlr, ~Instruction[2], ~Instruction[3], Instruction[4], Instruction[5], ~Instruction[6], Instruction[12], ~Instruction[13], Instruction[14], ~Instruction[30]);  // AND_Gate
  and and_20 (Srar, ~Instruction[2], ~Instruction[3], Instruction[4], Instruction[5], ~Instruction[6], Instruction[12], ~Instruction[13], Instruction[14], Instruction[30]);  // AND_Gate
  and and_21 (ORr, ~Instruction[2], ~Instruction[3], Instruction[4], Instruction[5], ~Instruction[6], ~Instruction[12], Instruction[13], Instruction[14], ~Instruction[30]);  // AND_Gate
  and and_22 (Andr, ~Instruction[2], ~Instruction[3], Instruction[4], Instruction[5], ~Instruction[6], Instruction[12], Instruction[13], Instruction[14], ~Instruction[30]);  // AND_Gate
  and and_23 (Srai, ~Instruction[2], ~Instruction[3], Instruction[4], ~Instruction[5], ~Instruction[6], Instruction[12], ~Instruction[13], Instruction[14], Instruction[30]);  // AND_Gate
  or or_3 (Sra, Srar, Srai);
  and and_24 (ORi, ~Instruction[2], ~Instruction[3], Instruction[4], ~Instruction[5], ~Instruction[6], ~Instruction[12], Instruction[13], Instruction[14], ~Instruction[30]);  // AND_Gate
  or or_4 (OR, ORr, ORi);
  and and_25 (Andi, ~Instruction[2], ~Instruction[3], Instruction[4], ~Instruction[5], ~Instruction[6], Instruction[12], Instruction[13], Instruction[14], ~Instruction[30]);  // AND_Gate
  or or_5 (And, Andr, Andi);
  nor nor_1 (nor_1_out, jal, jalr, Branch_enable);
  and and_26 (Addi, ~Instruction[2], ~Instruction[3], Instruction[4], ~Instruction[5], ~Instruction[6], ~Instruction[12], ~Instruction[13], ~Instruction[14], ~Instruction[30]);  // AND_Gate
  or or_6 (Add, Addr, Addi);
  or or_7 (SelBit[3], Sub, Sra);
  or or_8 (SelBit[2], Xor, Srl, Sra, OR, And);
  or or_9 (SelBit[1], Slt, Sltu, OR, And);
  or or_10 (SelBit[0], Sll, Sltu, Srl, Sra, And);
  and and_27 (Slli, ~Instruction[2], ~Instruction[3], Instruction[4], ~Instruction[5], ~Instruction[6], Instruction[12], ~Instruction[13], ~Instruction[14], ~Instruction[30]);  // AND_Gate
  or or_11 (Sll, Sllr, Slli);
  and and_28 (Slti, ~Instruction[2], ~Instruction[3], Instruction[4], ~Instruction[5], ~Instruction[6], ~Instruction[12], Instruction[13], ~Instruction[14], ~Instruction[30]);  // AND_Gate
  or or_12 (Slt, Sltr, Slti);
  and and_29 (Sltui, ~Instruction[2], ~Instruction[3], Instruction[4], ~Instruction[5], ~Instruction[6], Instruction[12], Instruction[13], ~Instruction[14], ~Instruction[30]);  // AND_Gate
  or or_13 (Sltu, Sltur, Sltui);
  and and_30 (Xori, ~Instruction[2], ~Instruction[3], Instruction[4], ~Instruction[5], ~Instruction[6], ~Instruction[12], ~Instruction[13], Instruction[14], ~Instruction[30]);  // AND_Gate
  or or_14 (Xor, Xorr, Xori);
  and and_31 (Srli, ~Instruction[2], ~Instruction[3], Instruction[4], ~Instruction[5], ~Instruction[6], Instruction[12], ~Instruction[13], Instruction[14], ~Instruction[30]);  // AND_Gate
  or or_15 (Srl, Srlr, Srli);
  or or_16 (Branch_enable, Breq, Bne, Blt, Bge, Bltu, Bgeu);
  Priority_Encoder #(.select(2)) priority_encoder_1 (
    .in0(nor_1_out), .in1(jal), .in2(jalr), .in3(Branch_enable), .out(selbit_for_mux));  // open: gs, en_out, en_in
  and and_32 (Breq, ~Instruction[2], ~Instruction[3], ~Instruction[4], Instruction[5], Instruction[6], ~Instruction[12], ~Instruction[13], ~Instruction[14], ~Instruction[30]);  // AND_Gate
  and and_33 (Bne, ~Instruction[2], ~Instruction[3], ~Instruction[4], Instruction[5], Instruction[6], Instruction[12], ~Instruction[13], ~Instruction[14], ~Instruction[30]);  // AND_Gate
  and and_34 (Blt, ~Instruction[2], ~Instruction[3], ~Instruction[4], Instruction[5], Instruction[6], ~Instruction[12], ~Instruction[13], Instruction[14], ~Instruction[30]);  // AND_Gate
  and and_35 (Bge, ~Instruction[2], ~Instruction[3], ~Instruction[4], Instruction[5], Instruction[6], Instruction[12], ~Instruction[13], Instruction[14], ~Instruction[30]);  // AND_Gate
  and and_36 (Bltu, ~Instruction[2], ~Instruction[3], ~Instruction[4], Instruction[5], Instruction[6], ~Instruction[12], Instruction[13], Instruction[14], ~Instruction[30]);  // AND_Gate
  and and_37 (Bgeu, ~Instruction[2], ~Instruction[3], ~Instruction[4], Instruction[5], Instruction[6], Instruction[12], Instruction[13], Instruction[14], ~Instruction[30]);  // AND_Gate
  or or_17 (wenb, lw, jal, lb, lh, Addr, Sub, Sllr, Sltr, Sltur, Xorr, Srlr, Srar, ORr, Andr, Srai, enable_for_auipc, ORi, Andi, Srli, Xori, Sltui, Slti, Slli, Addi, sw, sh, sb, lbu, lhu, jalr, lui_enable);
  or or_18 (rs2_imm_sel, lui_enable, jal, lb, lh, Addi, sw, sh, sb, Slli, Srai, enable_for_auipc, ORi, Andi, Srli, Xori, Sltui, Slti, lbu, lhu, jalr, lw);

  // Other names for the same wires on the sheet: auipc_wnable = enable_for_auipc; i0 = Instruction[2];
  //   i1 = Instruction[3]; i2 = Instruction[4]; i3 = Instruction[5]; i4 = Instruction[6]; i5 = Instruction[12];
  //   i6 = Instruction[13]; i7 = Instruction[14]; i8 = Instruction[30]; lui = lui_enable; out0 = SelBit[0];
  //   out1 = SelBit[1]; out2 = SelBit[2]; out3 = SelBit[3]

  // Notes on the sheet:
  //   Zainkhan5
  //   Zainkhan5
endmodule

module immediate_datapath (
  input  store,
  input  reset,
  input  [31:0] Inputinstruction,
  input  reset_for_reg_file,
  input  clk,
  input  [31:0] pc_4,
  input  [31:0] pc_for_auipc,
  output [31:0] ram_data,
  output [31:0] rs1_immedi_for_jalr,
  output [31:0] rd,
  output enable_for_imm_jal_branch,
  output [1:0] Selbit_for_mux,
  output [31:0] IMM_FOR_b_TYPE
);

  wire alu_1_output_branch_taken, and_1_out, and_2_out, control_unit_1_branch_enable,
       control_unit_1_rs2_imm_sel, control_unit_1_wenb, enable_for_auipc, jal_enable, load_enable,
       lui_enable, nor_1_out;
  wire [2:0] priority_encoder_1_out;
  wire [3:0] control_unit_1_selbit;
  wire [23:0] bit_extender_1_out;
  wire [31:0] alu_control_for_imm_1_output_for_datab, bit_extender_2_out, bit_extender_3_out,
       multiplexer_2_out, output_data_for_store, pc_imm_for_auipc, register_file_1_rs1out, rs2_data_to_save,
       shifter_1_out;

  Register_File register_file_1 (
    .RSI(Inputinstruction[19:15]), .RSI2(Inputinstruction[24:20]), .RDInstruction(Inputinstruction[11:7]),
    .reset(reset_for_reg_file), .clk(clk), .RDValue(multiplexer_2_out), .Write_Enable(control_unit_1_wenb),
    .RS1out(register_file_1_rs1out), .RS2out(rs2_data_to_save));
  Immediate_Generator immediate_generator_1 (.Inst_Input(Inputinstruction), .Immediate(IMM_FOR_b_TYPE));
  Control_Unit control_unit_1 (
    .Instruction(Inputinstruction), .SelBit(control_unit_1_selbit), .wenb(control_unit_1_wenb),
    .rs2_imm_sel(control_unit_1_rs2_imm_sel), .Enable_for_jal(jal_enable), .Load_Enable(load_enable),
    .Branch_enable(control_unit_1_branch_enable), .enable_for_auipc(enable_for_auipc),
    .selbit_for_mux(Selbit_for_mux), .lui_enable(lui_enable));
  Adder #(.width(32)) adder_1 (
    .a(register_file_1_rs1out), .b(IMM_FOR_b_TYPE), .out(rs1_immedi_for_jalr));  // open: cin, cout
  ALU_Control_for_Imm alu_control_for_imm_1 (
    .RS1(rs2_data_to_save), .IMMG_input(IMM_FOR_b_TYPE), .sel_bit_for_rs2_imm(control_unit_1_rs2_imm_sel),
    .output_for_dataB(alu_control_for_imm_1_output_for_datab));
  Shifter #(.width(32), .shift("lr")) shifter_1 (.in(rd), .\dist (5'b00010), .out(shifter_1_out));
  Bit_Extender #(.in_width(32), .out_width(24)) bit_extender_1 (.in(shifter_1_out), .out(bit_extender_1_out));
  ALU alu_1 (
    .dataA(register_file_1_rs1out), .dataB(alu_control_for_imm_1_output_for_datab),
    .selector(control_unit_1_selbit), .selbit_for_unsigned(control_unit_1_branch_enable), .dataD(rd),
    .output_branch_taken(alu_1_output_branch_taken));
  and and_1 (and_1_out, alu_1_output_branch_taken, control_unit_1_branch_enable);
  assign bit_extender_2_out = {{24{1'b0}}, rs2_data_to_save[7:0]};  // Bit_Extender bit_extender_2
  assign bit_extender_3_out = {{16{1'b0}}, rs2_data_to_save[15:0]};  // Bit_Extender bit_extender_3
  RAM #(.addrWidth(24), .dataWidth(32), .bus("separate")) ram_1 (
    .addr(bit_extender_1_out), .din(output_data_for_store), .data(ram_data), .str(store), .sel(1'b1),
    .clk(clk), .ld(load_enable), .clr(reset));
  Multiplexer #(.select(4), .width(32)) multiplexer_1 (
    .in0(rs2_data_to_save), .in2(bit_extender_3_out), .in4(bit_extender_2_out), .out(output_data_for_store),
    .sel(control_unit_1_selbit));  // open: in1, in3, in5, in6, in7, in8, in9, in10, in11, in12, in13, in14, in15, en
  Adder #(.width(32)) adder_2 (.a(pc_for_auipc), .b(IMM_FOR_b_TYPE), .out(pc_imm_for_auipc));  // open: cin, cout
  Priority_Encoder priority_encoder_1 (
    .in0(nor_1_out), .in1(load_enable), .in2(jal_enable), .in3(enable_for_auipc), .in4(lui_enable),
    .out(priority_encoder_1_out));  // open: in5, in6, in7, en_in, gs, en_out
  Multiplexer #(.select(3), .width(32)) multiplexer_2 (
    .in0(rd), .in1(ram_data), .in2(pc_4), .in3(pc_imm_for_auipc), .in4(IMM_FOR_b_TYPE),
    .out(multiplexer_2_out), .sel(priority_encoder_1_out));  // open: in5, in6, in7, en
  nor nor_1 (nor_1_out, load_enable, jal_enable);
  and and_2 (and_2_out, jal_enable, 1'b1);
  or or_1 (enable_for_imm_jal_branch, and_1_out, and_2_out);

  // Other names for the same wires on the sheet: RDI[4:0] = Inputinstruction[11:7];
  //   RS1[4:0] = Inputinstruction[19:15]; RS2[4:0] = Inputinstruction[24:20]
endmodule

// Alu control for immedtiate
module ALU_Control_for_Imm (
  input  [31:0] RS1,
  input  [31:0] IMMG_input,
  input  sel_bit_for_rs2_imm,
  output [31:0] output_for_dataB
);

  Multiplexer #(.width(32)) multiplexer_1 (
    .in0(RS1), .in1(IMMG_input), .out(output_for_dataB), .sel(sel_bit_for_rs2_imm));  // open: en
endmodule

module RS1_Immediate (
  input  [31:0] Rs1,
  input  [31:0] Imm,
  output [31:0] RS1_immediate
);

  Adder #(.width(32)) adder_1 (.a(Rs1), .b(Imm), .out(RS1_immediate));  // open: cin, cout
endmodule
